// Logisim project 1-Flip-Flop-JK.circ as structural Verilog: 2 circuits, main circuit flipflopjk
module flipflopjk (
  input  nPreset,
  input  J,
  input  K,
  input  nClear,
  output Q,
  output nQ
);

  wire clock_1_out, nand_1_out, nand_2_out, nand_3_out, nand_4_out, nand_5_out, nand_7_out, not_1_out,
       not_2_out, not_3_out;

  Clock clock_1 (.out(clock_1_out));
  nand nand_1 (nand_1_out, nQ, J, clock_1_out);
  not not_1 (not_1_out, nPreset);
  not not_2 (not_2_out, clock_1_out);
  not not_3 (not_3_out, nClear);
  nand nand_2 (nand_2_out, clock_1_out, K, Q);
  nand nand_3 (nand_3_out, not_1_out, nand_1_out, nand_4_out);
  nand nand_4 (nand_4_out, nand_3_out, nand_2_out, not_3_out);
  nand nand_5 (nand_5_out, nand_3_out, not_2_out);
  nand nand_6 (Q, nand_5_out, nQ);
  nand nand_7 (nand_7_out, not_2_out, nand_4_out);
  nand nand_8 (nQ, Q, nand_7_out);

  // Notes on the sheet:
  //   Flip-Flop-JK
  //   Este é um flip-flop jk, feito com preset e clear, aonde não podemos ligar ambos ao mesmo tempo.
endmodule

module jk_padrao (
  input  set,
  input  J,
  input  clock,
  input  K,
  input  reset,
  output Q,
  output Q_prime
);

  wire nand_1_out, nand_2_out, not_1_out, not_2_out;

  not not_1 (not_1_out, set);
  nand nand_1 (nand_1_out, J, clock, Q_prime);
  nand nand_2 (nand_2_out, Q, clock, K);
  not not_2 (not_2_out, reset);
  nand nand_3 (Q, not_1_out, nand_1_out, Q_prime);
  nand nand_4 (Q_prime, Q, nand_2_out, not_2_out);
endmodule
