// Logisim project 1-FlipFlpo-D.circ as structural Verilog: 3 circuits, main circuit flipflpd
module flipflpd (
  input  set,
  input  clock,
  input  data,
  input  reset,
  output out_5,
  output out_6
);

  wire nand_1_out, nand_2_out, nand_3_out, nand_4_out, not_1_out, not_2_out;

  not not_1 (not_1_out, set);
  not not_2 (not_2_out, reset);
  nand nand_1 (nand_1_out, not_1_out, nand_4_out, nand_2_out);
  nand nand_2 (nand_2_out, nand_1_out, clock, not_2_out);
  nand nand_3 (nand_3_out, nand_2_out, clock, nand_4_out);
  nand nand_4 (nand_4_out, nand_3_out, data, not_2_out);
  nand nand_5 (out_5, not_1_out, nand_2_out, out_6);
  nand nand_6 (out_6, out_5, nand_3_out, not_2_out);
endmodule

module flipflop_padrao (
  input  set,
  input  reset,
  output Q,
  output Q_minus
);

  nand nand_1 (Q, ~set, Q_minus);  // NAND_Gate
  nand nand_2 (Q_minus, Q, ~reset);  // NAND_Gate
endmodule

module flipflop_d_padrao (
  input  D,
  input  clock,
  output Q,
  output Q_prime
);

  wire nand_1_out, nand_2_out, not_1_out;

  nand nand_1 (nand_1_out, D, clock);
  not not_1 (not_1_out, D);
  nand nand_2 (nand_2_out, not_1_out, clock);
  nand nand_3 (Q, nand_1_out, Q_prime);
  nand nand_4 (Q_prime, Q, nand_2_out);
endmodule
