// Logisim project 2-multiplexador 4x1 1bit.circ as structural Verilog: 1 circuit, main circuit multiplexador
module multiplexador (
  input  S1,
  input  S2,
  input  D0,
  input  D1,
  input  D2,
  input  D3,
  output S
);

  wire and_1_out, and_2_out, and_3_out, and_4_out;

  and and_1 (and_1_out, D0, ~S2, ~S1);  // AND_Gate
  and and_2 (and_2_out, D1, ~S1, S2);  // AND_Gate
  or or_1 (S, and_1_out, and_2_out, and_3_out, and_4_out);
  and and_3 (and_3_out, D2, S2, ~S1);  // AND_Gate
  and and_4 (and_4_out, D3, S2, S1);
endmodule
