// Logisim project 4-somador-que-soma-com-4.circ as structural Verilog: 2 circuits, main circuit somador 8bits
module somador_8bits (
  input  [7:0] entrada,
  output [7:0] saida
);

  wire not_1_out, somador1bit_1_cout, somador1bit_2_cout, somador1bit_3_cout, somador1bit_4_cout,
       somador1bit_5_cout, somador1bit_6_cout, somador1bit_7_cout;

  somador1bit somador1bit_1 (.A(entrada[0]), .B(1'b0), .S(saida[0]), .Cout(somador1bit_1_cout), .Cin(1'b0));
  somador1bit somador1bit_2 (
    .A(entrada[1]), .B(1'b0), .S(saida[1]), .Cout(somador1bit_2_cout), .Cin(somador1bit_1_cout));
  somador1bit somador1bit_3 (
    .A(entrada[2]), .B(not_1_out), .S(saida[2]), .Cout(somador1bit_3_cout), .Cin(somador1bit_2_cout));
  not not_1 (not_1_out, 1'b0);
  somador1bit somador1bit_4 (
    .A(entrada[3]), .B(1'b0), .S(saida[3]), .Cout(somador1bit_4_cout), .Cin(somador1bit_3_cout));
  somador1bit somador1bit_5 (
    .A(entrada[4]), .B(1'b0), .S(saida[4]), .Cout(somador1bit_5_cout), .Cin(somador1bit_4_cout));
  somador1bit somador1bit_6 (
    .A(entrada[5]), .B(1'b0), .S(saida[5]), .Cout(somador1bit_6_cout), .Cin(somador1bit_5_cout));
  somador1bit somador1bit_7 (
    .A(entrada[6]), .B(1'b0), .S(saida[6]), .Cout(somador1bit_7_cout), .Cin(somador1bit_6_cout));
  somador1bit somador1bit_8 (.A(entrada[7]), .B(1'b0), .S(saida[7]), .Cin(somador1bit_7_cout));  // open: Cout
endmodule

module somador1bit (
  input  Cin,
  input  A,
  input  B,
  output S,
  output Cout
);

  wire and_1_out, and_2_out, and_3_out, xor_1_out;

  xor xor_1 (xor_1_out, A, B);
  and and_1 (and_1_out, A, B);
  and and_2 (and_2_out, B, Cin);
  and and_3 (and_3_out, A, Cin);
  xor xor_2 (S, xor_1_out, Cin);
  or or_1 (Cout, and_1_out, and_2_out, and_3_out);
endmodule
