// Logisim project 5-Memoria-Rom.circ as structural Verilog: 1 circuit, main circuit memoria rom
module memoria_rom (
  input  [2:0] key,
  output [7:0] saida
);

  wire and_1_out, and_2_out, and_3_out, and_4_out, and_5_out, and_6_out, and_7_out, and_8_out;

  and and_1 (and_1_out, ~key[2], ~key[1], ~key[0]);  // AND_Gate
  and and_2 (and_2_out, ~key[2], ~key[1], key[0]);  // AND_Gate
  and and_3 (and_3_out, ~key[2], key[1], ~key[0]);  // AND_Gate
  and and_4 (and_4_out, ~key[2], key[1], key[0]);  // AND_Gate
  and and_5 (and_5_out, key[2], ~key[1], ~key[0]);  // AND_Gate
  and and_6 (and_6_out, key[2], ~key[1], key[0]);  // AND_Gate
  and and_7 (and_7_out, key[2], key[1], ~key[0]);  // AND_Gate
  and and_8 (and_8_out, key[2], key[1], key[0]);
  or or_1 (saida[7], and_8_out, and_5_out, and_4_out, and_1_out);
  or or_2 (saida[5], and_8_out, and_7_out, and_4_out, and_1_out);
  or or_3 (saida[6], and_7_out, and_6_out, and_3_out, and_2_out);
  or or_4 (saida[4], and_8_out, and_7_out, and_5_out, and_2_out);
  or or_5 (saida[3], and_8_out, and_7_out, and_6_out, and_3_out);
  or or_6 (saida[2], and_8_out, and_6_out, and_5_out, and_3_out);
  or or_7 (saida[1], and_8_out, and_5_out, and_4_out, and_2_out);
  or or_8 (saida[0], and_8_out, and_6_out, and_3_out, and_1_out);
endmodule
