// Logisim project 6-Memoria-RAM.circ as structural Verilog: 7 circuits, main circuit MEMORIARAM
module MEMORIARAM (
  input  escrever,
  input  ler,
  input  [7:0] entrada,
  input  [2:0] chave,
  input  reset,
  output [7:0] saida
);

  wire and_1_out, and_2_out, clock_out;
  wire [7:0] demul_8x1_1_saida, mul_8x1_8bits_1_saida, registrador_8bit_1_out_4, registrador_8bit_2_out_4,
       registrador_8bit_3_out_4, registrador_8bit_4_out_4, registrador_8bit_5_out_4,
       registrador_8bit_6_out_4, registrador_8bit_7_out_4, registrador_8bit_8_out_4;

  Clock clock (.out(clock_out));
  and and_1 (and_1_out, clock_out, escrever);
  DEMUL_8x1 demul_8x1_1 (.chave(chave), .clock(and_1_out), .saida(demul_8x1_1_saida));
  registrador_8bit registrador_8bit_1 (
    .entrada(entrada), .clock(demul_8x1_1_saida[0]), .out_4(registrador_8bit_1_out_4), .reset(reset));
  registrador_8bit registrador_8bit_2 (
    .entrada(entrada), .clock(demul_8x1_1_saida[1]), .out_4(registrador_8bit_2_out_4), .reset(reset));
  registrador_8bit registrador_8bit_3 (
    .entrada(entrada), .clock(demul_8x1_1_saida[2]), .out_4(registrador_8bit_3_out_4), .reset(reset));
  registrador_8bit registrador_8bit_4 (
    .entrada(entrada), .clock(demul_8x1_1_saida[3]), .out_4(registrador_8bit_4_out_4), .reset(reset));
  registrador_8bit registrador_8bit_5 (
    .entrada(entrada), .clock(demul_8x1_1_saida[4]), .out_4(registrador_8bit_5_out_4), .reset(reset));
  registrador_8bit registrador_8bit_6 (
    .entrada(entrada), .clock(demul_8x1_1_saida[5]), .out_4(registrador_8bit_6_out_4), .reset(reset));
  registrador_8bit registrador_8bit_7 (
    .entrada(entrada), .clock(demul_8x1_1_saida[6]), .out_4(registrador_8bit_7_out_4), .reset(reset));
  registrador_8bit registrador_8bit_8 (
    .entrada(entrada), .clock(demul_8x1_1_saida[7]), .out_4(registrador_8bit_8_out_4), .reset(reset));
  and and_2 (and_2_out, clock_out, ler);
  registrador_8bit registrador_8bit_9 (
    .entrada(mul_8x1_8bits_1_saida), .clock(and_2_out), .out_4(saida), .reset(reset));
  MUL_8x1_8bits mul_8x1_8bits_1 (
    .in0(registrador_8bit_1_out_4), .in1(registrador_8bit_2_out_4), .in2(registrador_8bit_3_out_4),
    .in4(registrador_8bit_4_out_4), .in4_2(registrador_8bit_5_out_4), .in5(registrador_8bit_6_out_4),
    .in6(registrador_8bit_7_out_4), .in7(registrador_8bit_8_out_4), .chave(chave),
    .saida(mul_8x1_8bits_1_saida));
endmodule

module registrador_8bit (
  input  [7:0] entrada,
  input  reset,
  input  clock,
  output [7:0] out_4
);

  FlipFlopD flipflopd_1 (.set(1'b0), .out_5(out_4[3]), .clock(clock), .data(entrada[3]), .reset(reset));  // open: out_6
  FlipFlopD flipflopd_2 (.set(1'b0), .out_5(out_4[4]), .clock(clock), .data(entrada[4]), .reset(reset));  // open: out_6
  FlipFlopD flipflopd_3 (.set(1'b0), .out_5(out_4[5]), .clock(clock), .data(entrada[5]), .reset(reset));  // open: out_6
  FlipFlopD flipflopd_4 (.set(1'b0), .out_5(out_4[6]), .clock(clock), .data(entrada[6]), .reset(reset));  // open: out_6
  FlipFlopD flipflopd_5 (.set(1'b0), .out_5(out_4[7]), .clock(clock), .data(entrada[7]), .reset(reset));  // open: out_6
  FlipFlopD flipflopd_6 (.set(1'b0), .out_5(out_4[0]), .clock(clock), .data(entrada[0]), .reset(reset));  // open: out_6
  FlipFlopD flipflopd_7 (.set(1'b0), .out_5(out_4[1]), .clock(clock), .data(entrada[1]), .reset(reset));  // open: out_6
  FlipFlopD flipflopd_8 (.set(1'b0), .out_5(out_4[2]), .clock(clock), .data(entrada[2]), .reset(reset));  // open: out_6
endmodule

module DEMUL_8x1 (
  input  [2:0] chave,
  input  clock,
  output [7:0] saida
);

  and and_1 (saida[0], ~chave[2], ~chave[1], ~chave[0], clock);  // AND_Gate
  and and_2 (saida[1], ~chave[2], ~chave[1], chave[0], clock);  // AND_Gate
  and and_3 (saida[2], ~chave[2], chave[1], ~chave[0], clock);  // AND_Gate
  and and_4 (saida[3], ~chave[2], chave[1], chave[0], clock);  // AND_Gate
  and and_5 (saida[4], chave[2], ~chave[1], ~chave[0], clock);  // AND_Gate
  and and_6 (saida[5], chave[2], ~chave[1], chave[0], clock);  // AND_Gate
  and and_7 (saida[6], chave[2], chave[1], ~chave[0], clock);  // AND_Gate
  and and_8 (saida[7], chave[2], chave[1], chave[0], clock);
endmodule

module FlipFlopD (
  input  set,
  input  clock,
  input  data,
  input  reset,
  output out_5,
  output out_6
);

  wire nand_1_out, nand_2_out, nand_3_out, nand_4_out, not_1_out, not_2_out;

  not not_1 (not_1_out, set);
  not not_2 (not_2_out, reset);
  nand nand_1 (nand_1_out, not_1_out, nand_4_out, nand_2_out);
  nand nand_2 (nand_2_out, nand_1_out, clock, not_2_out);
  nand nand_3 (nand_3_out, nand_2_out, clock, nand_4_out);
  nand nand_4 (nand_4_out, nand_3_out, data, not_2_out);
  nand nand_5 (out_5, not_1_out, nand_2_out, out_6);
  nand nand_6 (out_6, out_5, nand_3_out, not_2_out);
endmodule

module MUL_2x1_8bits (
  input  [7:0] entrada,
  input  [7:0] entrada_2,
  input  cahve,
  output [7:0] out_4
);

  MUL_2x1_2bits mul_2x1_2bits_1 (.in_1(entrada[0]), .in_3(cahve), .out_4(out_4[0]), .in_2(entrada_2[0]));
  MUL_2x1_2bits mul_2x1_2bits_2 (.in_1(entrada[1]), .in_3(cahve), .out_4(out_4[1]), .in_2(entrada_2[1]));
  MUL_2x1_2bits mul_2x1_2bits_3 (.in_1(entrada[2]), .in_3(cahve), .out_4(out_4[2]), .in_2(entrada_2[2]));
  MUL_2x1_2bits mul_2x1_2bits_4 (.in_1(entrada[3]), .in_3(cahve), .out_4(out_4[3]), .in_2(entrada_2[3]));
  MUL_2x1_2bits mul_2x1_2bits_5 (.in_1(entrada[4]), .in_3(cahve), .out_4(out_4[4]), .in_2(entrada_2[4]));
  MUL_2x1_2bits mul_2x1_2bits_6 (.in_1(entrada[5]), .in_3(cahve), .out_4(out_4[5]), .in_2(entrada_2[5]));
  MUL_2x1_2bits mul_2x1_2bits_7 (.in_1(entrada[6]), .in_3(cahve), .out_4(out_4[6]), .in_2(entrada_2[6]));
  MUL_2x1_2bits mul_2x1_2bits_8 (.in_1(entrada[7]), .in_3(cahve), .out_4(out_4[7]), .in_2(entrada_2[7]));
endmodule

module MUL_2x1_2bits (
  input  in_1,
  input  in_2,
  input  in_3,
  output out_4
);

  wire and_1_out, and_2_out;

  and and_1 (and_1_out, in_1, ~in_3);  // AND_Gate
  and and_2 (and_2_out, in_2, in_3);
  or or_1 (out_4, and_1_out, and_2_out);
endmodule

module MUL_8x1_8bits (
  input  [7:0] in0,
  input  [7:0] in1,
  input  [7:0] in2,
  input  [7:0] in4,
  input  [7:0] in4_2,
  input  [7:0] in5,
  input  [7:0] in6,
  input  [7:0] in7,
  input  [2:0] chave,
  output [7:0] saida
);

  wire [7:0] mul_2x1_8bits_1_out_4, mul_2x1_8bits_2_out_4, mul_2x1_8bits_3_out_4, mul_2x1_8bits_4_out_4,
       mul_2x1_8bits_5_out_4, mul_2x1_8bits_6_out_4;

  MUL_2x1_8bits mul_2x1_8bits_1 (.entrada(in0), .entrada_2(in1), .out_4(mul_2x1_8bits_1_out_4), .cahve(chave[0]));
  MUL_2x1_8bits mul_2x1_8bits_2 (.entrada(in2), .entrada_2(in4), .out_4(mul_2x1_8bits_2_out_4), .cahve(chave[0]));
  MUL_2x1_8bits mul_2x1_8bits_3 (.entrada(in4_2), .entrada_2(in5), .out_4(mul_2x1_8bits_3_out_4), .cahve(chave[0]));
  MUL_2x1_8bits mul_2x1_8bits_4 (.entrada(in6), .entrada_2(in7), .out_4(mul_2x1_8bits_4_out_4), .cahve(chave[0]));
  MUL_2x1_8bits mul_2x1_8bits_5 (
    .entrada(mul_2x1_8bits_1_out_4), .entrada_2(mul_2x1_8bits_2_out_4), .out_4(mul_2x1_8bits_5_out_4),
    .cahve(chave[1]));
  MUL_2x1_8bits mul_2x1_8bits_6 (
    .entrada(mul_2x1_8bits_3_out_4), .entrada_2(mul_2x1_8bits_4_out_4), .out_4(mul_2x1_8bits_6_out_4),
    .cahve(chave[1]));
  MUL_2x1_8bits mul_2x1_8bits_7 (
    .entrada(mul_2x1_8bits_5_out_4), .entrada_2(mul_2x1_8bits_6_out_4), .out_4(saida), .cahve(chave[2]));
endmodule
