// Logisim project 7-Banco-de-Resistradores.circ as structural Verilog: 9 circuits, main circuit banco de registradores
module banco_de_registradores (
  input  reset,
  input  [7:0] WS3,
  input  [3:0] A3,
  input  [3:0] A1,
  input  [3:0] A2,
  output [7:0] RD1,
  output [7:0] RD2
);

  wire clock_1_out, dem_1x2_1_out_3, dem_1x2_1_out_4;
  wire [7:0] dem_1x8_1_saida, dem_1x8_2_saida, registrado_8_bits_1_out_4, registrado_8_bits_2_out_4,
       registrado_8_bits_3_out_4, registrado_8_bits_4_out_4, registrado_8_bits_5_out_4,
       registrado_8_bits_6_out_4, registrado_8_bits_7_out_4, registrado_8_bits_8_out_4,
       registrado_8_bits_9_out_4, registrado_8_bits_10_out_4, registrado_8_bits_11_out_4,
       registrado_8_bits_12_out_4, registrado_8_bits_13_out_4, registrado_8_bits_14_out_4,
       registrado_8_bits_15_out_4, registrado_8_bits_16_out_4;

  DEM_1x2 dem_1x2_1 (.in_1(A3[3]), .in_2(clock_1_out), .out_3(dem_1x2_1_out_3), .out_4(dem_1x2_1_out_4));
  Clock clock_1 (.out(clock_1_out));
  DEM_1x8 dem_1x8_1 (.chave(A3[2:0]), .clock(dem_1x2_1_out_3), .saida(dem_1x8_1_saida));
  DEM_1x8 dem_1x8_2 (.chave(A3[2:0]), .clock(dem_1x2_1_out_4), .saida(dem_1x8_2_saida));
  registrado_8_bits registrado_8_bits_1 (
    .in_1(WS3), .clock(dem_1x8_1_saida[0]), .out_4(registrado_8_bits_1_out_4), .in_2(reset));
  registrado_8_bits registrado_8_bits_2 (
    .in_1(WS3), .clock(dem_1x8_1_saida[4]), .out_4(registrado_8_bits_2_out_4), .in_2(reset));
  registrado_8_bits registrado_8_bits_3 (
    .in_1(WS3), .clock(dem_1x8_2_saida[0]), .out_4(registrado_8_bits_3_out_4), .in_2(reset));
  registrado_8_bits registrado_8_bits_4 (
    .in_1(WS3), .clock(dem_1x8_2_saida[4]), .out_4(registrado_8_bits_4_out_4), .in_2(reset));
  registrado_8_bits registrado_8_bits_5 (
    .in_1(WS3), .clock(dem_1x8_1_saida[1]), .out_4(registrado_8_bits_5_out_4), .in_2(reset));
  registrado_8_bits registrado_8_bits_6 (
    .in_1(WS3), .clock(dem_1x8_1_saida[5]), .out_4(registrado_8_bits_6_out_4), .in_2(reset));
  registrado_8_bits registrado_8_bits_7 (
    .in_1(WS3), .clock(dem_1x8_2_saida[1]), .out_4(registrado_8_bits_7_out_4), .in_2(reset));
  registrado_8_bits registrado_8_bits_8 (
    .in_1(WS3), .clock(dem_1x8_2_saida[5]), .out_4(registrado_8_bits_8_out_4), .in_2(reset));
  registrado_8_bits registrado_8_bits_9 (
    .in_1(WS3), .clock(dem_1x8_1_saida[2]), .out_4(registrado_8_bits_9_out_4), .in_2(reset));
  registrado_8_bits registrado_8_bits_10 (
    .in_1(WS3), .clock(dem_1x8_1_saida[6]), .out_4(registrado_8_bits_10_out_4), .in_2(reset));
  registrado_8_bits registrado_8_bits_11 (
    .in_1(WS3), .clock(dem_1x8_2_saida[2]), .out_4(registrado_8_bits_11_out_4), .in_2(reset));
  registrado_8_bits registrado_8_bits_12 (
    .in_1(WS3), .clock(dem_1x8_2_saida[6]), .out_4(registrado_8_bits_12_out_4), .in_2(reset));
  registrado_8_bits registrado_8_bits_13 (
    .in_1(WS3), .clock(dem_1x8_1_saida[3]), .out_4(registrado_8_bits_13_out_4), .in_2(reset));
  registrado_8_bits registrado_8_bits_14 (
    .in_1(WS3), .clock(dem_1x8_1_saida[7]), .out_4(registrado_8_bits_14_out_4), .in_2(reset));
  registrado_8_bits registrado_8_bits_15 (
    .in_1(WS3), .clock(dem_1x8_2_saida[3]), .out_4(registrado_8_bits_15_out_4), .in_2(reset));
  registrado_8_bits registrado_8_bits_16 (
    .in_1(WS3), .clock(dem_1x8_2_saida[7]), .out_4(registrado_8_bits_16_out_4), .in_2(reset));
  MUL_16x1_8bits mul_16x1_8bits_1 (
    .in_1(registrado_8_bits_1_out_4), .in_2(registrado_8_bits_5_out_4), .in_3(registrado_8_bits_9_out_4),
    .in_4(registrado_8_bits_13_out_4), .in_5(registrado_8_bits_2_out_4), .in_6(registrado_8_bits_6_out_4),
    .in_7(registrado_8_bits_10_out_4), .in_8(registrado_8_bits_14_out_4), .in_9(registrado_8_bits_3_out_4),
    .in_10(registrado_8_bits_7_out_4), .in_11(registrado_8_bits_11_out_4),
    .in_12(registrado_8_bits_15_out_4), .in_13(registrado_8_bits_4_out_4), .in_14(registrado_8_bits_8_out_4),
    .in_15(registrado_8_bits_12_out_4), .in_16(registrado_8_bits_16_out_4), .key(A1), .out_18(RD1));
  MUL_16x1_8bits mul_16x1_8bits_2 (
    .in_1(registrado_8_bits_1_out_4), .in_2(registrado_8_bits_5_out_4), .in_3(registrado_8_bits_9_out_4),
    .in_4(registrado_8_bits_13_out_4), .in_5(registrado_8_bits_2_out_4), .in_6(registrado_8_bits_6_out_4),
    .in_7(registrado_8_bits_10_out_4), .in_8(registrado_8_bits_14_out_4), .in_9(registrado_8_bits_3_out_4),
    .in_10(registrado_8_bits_7_out_4), .in_11(registrado_8_bits_11_out_4),
    .in_12(registrado_8_bits_15_out_4), .in_13(registrado_8_bits_4_out_4), .in_14(registrado_8_bits_8_out_4),
    .in_15(registrado_8_bits_12_out_4), .in_16(registrado_8_bits_16_out_4), .key(A2), .out_18(RD2));
endmodule

module flipflop_D (
  input  set,
  input  clock,
  input  data,
  input  reset,
  output out_5,
  output out_6
);

  wire nand_1_out, nand_2_out, nand_3_out, nand_4_out, not_1_out, not_2_out;

  not not_1 (not_1_out, set);
  not not_2 (not_2_out, reset);
  nand nand_1 (nand_1_out, not_1_out, nand_4_out, nand_2_out);
  nand nand_2 (nand_2_out, nand_1_out, clock, not_2_out);
  nand nand_3 (nand_3_out, nand_2_out, clock, nand_4_out);
  nand nand_4 (nand_4_out, nand_3_out, data, not_2_out);
  nand nand_5 (out_5, not_1_out, nand_2_out, out_6);
  nand nand_6 (out_6, out_5, nand_3_out, not_2_out);
endmodule

module registrado_8_bits (
  input  [7:0] in_1,
  input  in_2,
  input  clock,
  output [7:0] out_4
);

  FlipFlopD flipflopd_1 (.set(1'b0), .out_5(out_4[3]), .clock(clock), .data(in_1[3]), .reset(in_2));  // open: out_6
  FlipFlopD flipflopd_2 (.set(1'b0), .out_5(out_4[4]), .clock(clock), .data(in_1[4]), .reset(in_2));  // open: out_6
  FlipFlopD flipflopd_3 (.set(1'b0), .out_5(out_4[5]), .clock(clock), .data(in_1[5]), .reset(in_2));  // open: out_6
  FlipFlopD flipflopd_4 (.set(1'b0), .out_5(out_4[6]), .clock(clock), .data(in_1[6]), .reset(in_2));  // open: out_6
  FlipFlopD flipflopd_5 (.set(1'b0), .out_5(out_4[7]), .clock(clock), .data(in_1[7]), .reset(in_2));  // open: out_6
  FlipFlopD flipflopd_6 (.set(1'b0), .out_5(out_4[0]), .clock(clock), .data(in_1[0]), .reset(in_2));  // open: out_6
  FlipFlopD flipflopd_7 (.set(1'b0), .out_5(out_4[1]), .clock(clock), .data(in_1[1]), .reset(in_2));  // open: out_6
  FlipFlopD flipflopd_8 (.set(1'b0), .out_5(out_4[2]), .clock(clock), .data(in_1[2]), .reset(in_2));  // open: out_6
endmodule

module DEM_1x8 (
  input  [2:0] chave,
  input  clock,
  output [7:0] saida
);

  and and_1 (saida[0], ~chave[2], ~chave[1], ~chave[0], clock);  // AND_Gate
  and and_2 (saida[1], ~chave[2], ~chave[1], chave[0], clock);  // AND_Gate
  and and_3 (saida[2], ~chave[2], chave[1], ~chave[0], clock);  // AND_Gate
  and and_4 (saida[3], ~chave[2], chave[1], chave[0], clock);  // AND_Gate
  and and_5 (saida[4], chave[2], ~chave[1], ~chave[0], clock);  // AND_Gate
  and and_6 (saida[5], chave[2], ~chave[1], chave[0], clock);  // AND_Gate
  and and_7 (saida[6], chave[2], chave[1], ~chave[0], clock);  // AND_Gate
  and and_8 (saida[7], chave[2], chave[1], chave[0], clock);
endmodule

module DEM_1x2 (
  input  in_1,
  input  in_2,
  output out_3,
  output out_4
);

  and and_1 (out_3, in_2, ~in_1);  // AND_Gate
  and and_2 (out_4, in_2, in_1);
endmodule

module MUL_2x1_2bits (
  input  in_1,
  input  in_2,
  input  in_3,
  output out_4
);

  wire and_1_out, and_2_out;

  and and_1 (and_1_out, in_1, ~in_3);  // AND_Gate
  and and_2 (and_2_out, in_2, in_3);
  or or_1 (out_4, and_1_out, and_2_out);
endmodule

module MUL_2x1_8bits (
  input  [7:0] entrada,
  input  [7:0] entrada_2,
  input  cahve,
  output [7:0] out_4
);

  _6_Memoria_RAM_MUL_2x1_2bits mul_2x1_2bits_1 (.in_1(entrada[0]), .in_3(cahve), .out_4(out_4[0]), .in_2(entrada_2[0]));
  _6_Memoria_RAM_MUL_2x1_2bits mul_2x1_2bits_2 (.in_1(entrada[1]), .in_3(cahve), .out_4(out_4[1]), .in_2(entrada_2[1]));
  _6_Memoria_RAM_MUL_2x1_2bits mul_2x1_2bits_3 (.in_1(entrada[2]), .in_3(cahve), .out_4(out_4[2]), .in_2(entrada_2[2]));
  _6_Memoria_RAM_MUL_2x1_2bits mul_2x1_2bits_4 (.in_1(entrada[3]), .in_3(cahve), .out_4(out_4[3]), .in_2(entrada_2[3]));
  _6_Memoria_RAM_MUL_2x1_2bits mul_2x1_2bits_5 (.in_1(entrada[4]), .in_3(cahve), .out_4(out_4[4]), .in_2(entrada_2[4]));
  _6_Memoria_RAM_MUL_2x1_2bits mul_2x1_2bits_6 (.in_1(entrada[5]), .in_3(cahve), .out_4(out_4[5]), .in_2(entrada_2[5]));
  _6_Memoria_RAM_MUL_2x1_2bits mul_2x1_2bits_7 (.in_1(entrada[6]), .in_3(cahve), .out_4(out_4[6]), .in_2(entrada_2[6]));
  _6_Memoria_RAM_MUL_2x1_2bits mul_2x1_2bits_8 (.in_1(entrada[7]), .in_3(cahve), .out_4(out_4[7]), .in_2(entrada_2[7]));
endmodule

module MUL_8x1_8bits (
  input  [7:0] in0,
  input  [7:0] in1,
  input  [7:0] in2,
  input  [7:0] in4,
  input  [7:0] in4_2,
  input  [7:0] in5,
  input  [7:0] in6,
  input  [7:0] in7,
  input  [2:0] chave,
  output [7:0] saida
);

  wire [7:0] mul_2x1_8bits_1_out_4, mul_2x1_8bits_2_out_4, mul_2x1_8bits_3_out_4, mul_2x1_8bits_4_out_4,
       mul_2x1_8bits_5_out_4, mul_2x1_8bits_6_out_4;

  _6_Memoria_RAM_MUL_2x1_8bits mul_2x1_8bits_1 (
    .entrada(in0), .entrada_2(in1), .out_4(mul_2x1_8bits_1_out_4), .cahve(chave[0]));
  _6_Memoria_RAM_MUL_2x1_8bits mul_2x1_8bits_2 (
    .entrada(in2), .entrada_2(in4), .out_4(mul_2x1_8bits_2_out_4), .cahve(chave[0]));
  _6_Memoria_RAM_MUL_2x1_8bits mul_2x1_8bits_3 (
    .entrada(in4_2), .entrada_2(in5), .out_4(mul_2x1_8bits_3_out_4), .cahve(chave[0]));
  _6_Memoria_RAM_MUL_2x1_8bits mul_2x1_8bits_4 (
    .entrada(in6), .entrada_2(in7), .out_4(mul_2x1_8bits_4_out_4), .cahve(chave[0]));
  _6_Memoria_RAM_MUL_2x1_8bits mul_2x1_8bits_5 (
    .entrada(mul_2x1_8bits_1_out_4), .entrada_2(mul_2x1_8bits_2_out_4), .out_4(mul_2x1_8bits_5_out_4),
    .cahve(chave[1]));
  _6_Memoria_RAM_MUL_2x1_8bits mul_2x1_8bits_6 (
    .entrada(mul_2x1_8bits_3_out_4), .entrada_2(mul_2x1_8bits_4_out_4), .out_4(mul_2x1_8bits_6_out_4),
    .cahve(chave[1]));
  _6_Memoria_RAM_MUL_2x1_8bits mul_2x1_8bits_7 (
    .entrada(mul_2x1_8bits_5_out_4), .entrada_2(mul_2x1_8bits_6_out_4), .out_4(saida), .cahve(chave[2]));
endmodule

module MUL_16x1_8bits (
  input  [7:0] in_1,
  input  [7:0] in_2,
  input  [7:0] in_3,
  input  [7:0] in_4,
  input  [7:0] in_5,
  input  [7:0] in_6,
  input  [7:0] in_7,
  input  [7:0] in_8,
  input  [7:0] in_9,
  input  [7:0] in_10,
  input  [7:0] in_11,
  input  [7:0] in_12,
  input  [7:0] in_13,
  input  [7:0] in_14,
  input  [7:0] in_15,
  input  [7:0] in_16,
  input  [3:0] key,
  output [7:0] out_18
);

  wire [7:0] mul_8x1_8bits_1_saida, mul_8x1_8bits_2_saida;

  MUL_8x1_8bits mul_8x1_8bits_1 (
    .in0(in_1), .in1(in_2), .in2(in_3), .in4(in_4), .in4_2(in_5), .in5(in_6), .in6(in_7), .in7(in_8),
    .chave(key[2:0]), .saida(mul_8x1_8bits_1_saida));
  MUL_8x1_8bits mul_8x1_8bits_2 (
    .in0(in_9), .in1(in_10), .in2(in_11), .in4(in_12), .in4_2(in_13), .in5(in_14), .in6(in_15), .in7(in_16),
    .chave(key[2:0]), .saida(mul_8x1_8bits_2_saida));
  MUL_2x1_8bits mul_2x1_8bits_1 (
    .entrada(mul_8x1_8bits_1_saida), .entrada_2(mul_8x1_8bits_2_saida), .cahve(key[3]), .out_4(out_18));
endmodule
