// Logisim project 8-Somador 8bits.circ as structural Verilog: 3 circuits, main circuit somador 8 bits
module somador_8_bits (
  input  [7:0] entrada_A,
  input  [7:0] Entrada_B,
  output [7:0] saida
);

  wire somador_completo_1_co, somador_completo_2_co, somador_completo_3_co, somador_completo_4_co,
       somador_completo_5_co, somador_completo_6_co, somador_completo_7_co;

  somador_completo somador_completo_1 (
    .ci(1'b0), .a(entrada_A[0]), .b(Entrada_B[0]), .s(saida[0]), .co(somador_completo_1_co));
  somador_completo somador_completo_2 (
    .ci(somador_completo_1_co), .a(entrada_A[1]), .b(Entrada_B[1]), .s(saida[1]), .co(somador_completo_2_co));
  somador_completo somador_completo_3 (
    .ci(somador_completo_2_co), .a(entrada_A[2]), .b(Entrada_B[2]), .s(saida[2]), .co(somador_completo_3_co));
  somador_completo somador_completo_4 (
    .ci(somador_completo_3_co), .a(entrada_A[3]), .b(Entrada_B[3]), .s(saida[3]), .co(somador_completo_4_co));
  somador_completo somador_completo_5 (
    .ci(somador_completo_4_co), .a(entrada_A[4]), .b(Entrada_B[4]), .s(saida[4]), .co(somador_completo_5_co));
  somador_completo somador_completo_6 (
    .ci(somador_completo_5_co), .a(entrada_A[5]), .b(Entrada_B[5]), .s(saida[5]), .co(somador_completo_6_co));
  somador_completo somador_completo_7 (
    .ci(somador_completo_6_co), .a(entrada_A[6]), .b(Entrada_B[6]), .s(saida[6]), .co(somador_completo_7_co));
  somador_completo somador_completo_8 (
    .ci(somador_completo_7_co), .a(entrada_A[7]), .b(Entrada_B[7]), .s(saida[7]));  // open: co
endmodule

module half (
  input  in_1,
  input  in_2,
  output out_3,
  output out_4
);

  xor xor_1 (out_3, in_1, in_2);
  and and_1 (out_4, in_1, in_2);
endmodule

module somador_completo (
  input  ci,
  input  a,
  input  b,
  output s,
  output co
);

  wire half_1_out_3, half_1_out_4, half_2_out_4;

  half half_1 (.in_1(a), .in_2(b), .out_3(half_1_out_3), .out_4(half_1_out_4));
  half half_2 (.in_1(ci), .in_2(half_1_out_3), .out_3(s), .out_4(half_2_out_4));
  or or_1 (co, half_2_out_4, half_1_out_4);
endmodule
