// Logisim project 9-Detector101.circ as structural Verilog: 1 circuit, main circuit main
module main (
  input  [7:0] in_1,
  output out_2
);

  wire and_1_out, and_2_out, and_3_out, and_4_out, and_5_out, and_6_out;

  and and_1 (and_1_out, in_1[0], ~in_1[1], in_1[2]);  // AND_Gate
  and and_2 (and_2_out, in_1[1], ~in_1[2], in_1[3]);  // AND_Gate
  and and_3 (and_3_out, in_1[2], ~in_1[3], in_1[4]);  // AND_Gate
  and and_4 (and_4_out, in_1[3], ~in_1[4], in_1[5]);  // AND_Gate
  and and_5 (and_5_out, in_1[4], ~in_1[5], in_1[6]);  // AND_Gate
  and and_6 (and_6_out, in_1[5], ~in_1[6], in_1[7]);  // AND_Gate
  or or_1 (out_2, and_1_out, and_2_out, and_3_out, and_4_out, and_5_out, and_6_out);
endmodule
