// Logisim project 10-Ula.circ as structural Verilog: 8 circuits, main circuit ula
module ula (
  input  [7:0] A,
  input  [7:0] B,
  input  [3:0] CHAVE,
  output [7:0] SAIDA,
  output overflow
);

  wire somadorsubtrador_1_out_5, somadorsubtrador_2_out_5;
  wire [7:0] and_1_out, deslocador_2bits_1_out_3, deslocador_2bits_2_out_3, deslocador_2bits_3_out_3,
       deslocador_2bits_4_out_3, mul_8x1_8bits_1_saida, mul_8x1_8bits_2_saida, nand_1_out, nor_1_out,
       not_1_out, not_2_out, or_1_out, somadorsubtrador_1_out_4, somadorsubtrador_2_out_4, xor_1_out;

  assign and_1_out = A & B;  // AND_Gate and_1, 8 bits wide
  assign or_1_out = A | B;  // OR_Gate or_1, 8 bits wide
  assign not_1_out = ~A;  // NOT_Gate not_1, 8 bits wide
  assign not_2_out = ~B;  // NOT_Gate not_2, 8 bits wide
  assign nor_1_out = ~(A | B);  // NOR_Gate nor_1, 8 bits wide
  assign nand_1_out = ~(A & B);  // NAND_Gate nand_1, 8 bits wide
  assign xor_1_out = A ^ B;  // XOR_Gate xor_1, 8 bits wide
  deslocador_2bits deslocador_2bits_1 (.in_1(A), .ritgh_left(1'b0), .out_3(deslocador_2bits_1_out_3));
  deslocador_2bits deslocador_2bits_2 (.in_1(B), .ritgh_left(1'b0), .out_3(deslocador_2bits_2_out_3));
  deslocador_2bits deslocador_2bits_3 (.in_1(A), .ritgh_left(1'b1), .out_3(deslocador_2bits_3_out_3));
  deslocador_2bits deslocador_2bits_4 (.in_1(B), .ritgh_left(1'b1), .out_3(deslocador_2bits_4_out_3));
  somadorsubtrador somadorsubtrador_1 (
    .m(1'b0), .out_4(somadorsubtrador_1_out_4), .out_5(somadorsubtrador_1_out_5), .in_2(A), .in_3(B));
  somadorsubtrador somadorsubtrador_2 (
    .m(1'b1), .out_4(somadorsubtrador_2_out_4), .out_5(somadorsubtrador_2_out_5), .in_2(A), .in_3(B));
  MUL_8x1_8bits mul_8x1_8bits_1 (
    .in0(and_1_out), .in1(or_1_out), .in2(not_1_out), .in4(not_2_out), .in4_2(nor_1_out), .in5(nand_1_out),
    .in6(xor_1_out), .in7(deslocador_2bits_1_out_3), .chave(CHAVE[2:0]), .saida(mul_8x1_8bits_1_saida));
  MUL_8x1_8bits mul_8x1_8bits_2 (
    .in0(deslocador_2bits_2_out_3), .in1(deslocador_2bits_3_out_3), .in2(deslocador_2bits_4_out_3),
    .in4(somadorsubtrador_1_out_4), .in4_2(somadorsubtrador_2_out_4), .chave(CHAVE[2:0]),
    .saida(mul_8x1_8bits_2_saida));  // open: in5, in6, in7
  MUL_2x1_8bits mul_2x1_8bits_1 (
    .entrada(mul_8x1_8bits_1_saida), .entrada_2(mul_8x1_8bits_2_saida), .out_4(SAIDA), .cahve(CHAVE[3]));
  MUL_2x1_2bits mul_2x1_2bits_1 (
    .in_1(somadorsubtrador_1_out_5), .in_3(CHAVE[2]), .out_4(overflow), .in_2(somadorsubtrador_2_out_5));

  // Notes on the sheet:
  //   0000 - AND
  //   0001 - OR
  //   0010 - NOT A
  //   0011 - NOT B
  //   0100 - NOR
  //   0101 - NAND
  //   0110 - XOR
  //   0111 - SHIFT LEFT A
  //   1000 - SHIFT LEFT B
  //   1001 - SHIFT RIGHT A
  //   1010 - SHIFT RIGHT B
  //   1011 - SOMA
  //   1100 - SUBTRAÇÃO
endmodule

module half (
  input  in_1,
  input  in_2,
  output out_3,
  output out_4
);

  xor xor_1 (out_3, in_1, in_2);
  and and_1 (out_4, in_1, in_2);
endmodule

module somador_completo (
  input  ci,
  input  a,
  input  b,
  output s,
  output co
);

  wire half_1_out_3, half_1_out_4, half_2_out_4;

  half half_1 (.in_1(a), .in_2(b), .out_3(half_1_out_3), .out_4(half_1_out_4));
  half half_2 (.in_1(ci), .in_2(half_1_out_3), .out_3(s), .out_4(half_2_out_4));
  or or_1 (co, half_2_out_4, half_1_out_4);
endmodule

module somador_8bits (
  input  [7:0] in_1,
  input  co,
  input  [7:0] in_3,
  output [7:0] out_4
);

  wire somador_completo_1_co, somador_completo_2_co, somador_completo_3_co, somador_completo_4_co,
       somador_completo_5_co, somador_completo_6_co, somador_completo_7_co;

  somador_completo somador_completo_1 (.ci(co), .a(in_1[0]), .b(in_3[0]), .s(out_4[0]), .co(somador_completo_1_co));
  somador_completo somador_completo_2 (
    .ci(somador_completo_1_co), .a(in_1[1]), .b(in_3[1]), .s(out_4[1]), .co(somador_completo_2_co));
  somador_completo somador_completo_3 (
    .ci(somador_completo_2_co), .a(in_1[2]), .b(in_3[2]), .s(out_4[2]), .co(somador_completo_3_co));
  somador_completo somador_completo_4 (
    .ci(somador_completo_3_co), .a(in_1[3]), .b(in_3[3]), .s(out_4[3]), .co(somador_completo_4_co));
  somador_completo somador_completo_5 (
    .ci(somador_completo_4_co), .a(in_1[4]), .b(in_3[4]), .s(out_4[4]), .co(somador_completo_5_co));
  somador_completo somador_completo_6 (
    .ci(somador_completo_5_co), .a(in_1[5]), .b(in_3[5]), .s(out_4[5]), .co(somador_completo_6_co));
  somador_completo somador_completo_7 (
    .ci(somador_completo_6_co), .a(in_1[6]), .b(in_3[6]), .s(out_4[6]), .co(somador_completo_7_co));
  somador_completo somador_completo_8 (.ci(somador_completo_7_co), .a(in_1[7]), .b(in_3[7]), .s(out_4[7]));  // open: co
endmodule

module overflow (
  input  ci,
  input  a,
  input  b,
  output out_4,
  output out_5,
  output out_6
);

  wire half_1_out_3, half_1_out_4, half_2_out_4;

  half half_1 (.in_1(a), .in_2(b), .out_3(half_1_out_3), .out_4(half_1_out_4));
  half half_2 (.in_1(ci), .in_2(half_1_out_3), .out_3(out_4), .out_4(half_2_out_4));
  or or_1 (out_5, half_2_out_4, half_1_out_4);
  xor xor_1 (out_6, out_5, ci);
endmodule

module somadorsubtrador (
  input  m,
  input  [7:0] in_2,
  input  [7:0] in_3,
  output [7:0] out_4,
  output out_5
);

  wire somador_completo_1_co, somador_completo_2_co, somador_completo_3_co, somador_completo_4_co,
       somador_completo_5_co, somador_completo_6_co, somador_completo_7_co, somador_completo_8_co, xor_1_out,
       xor_2_out, xor_3_out, xor_4_out, xor_5_out, xor_6_out, xor_7_out, xor_8_out;

  xor xor_1 (xor_1_out, in_3[0], m);
  xor xor_2 (xor_2_out, in_3[1], m);
  xor xor_3 (xor_3_out, in_3[2], m);
  xor xor_4 (xor_4_out, in_3[3], m);
  xor xor_5 (xor_5_out, in_3[4], m);
  xor xor_6 (xor_6_out, in_3[5], m);
  xor xor_7 (xor_7_out, in_3[6], m);
  xor xor_8 (xor_8_out, in_3[7], m);
  somador_completo somador_completo_1 (.ci(m), .a(in_2[0]), .b(xor_1_out), .s(out_4[0]), .co(somador_completo_1_co));
  somador_completo somador_completo_2 (
    .ci(somador_completo_1_co), .a(in_2[1]), .b(xor_2_out), .s(out_4[1]), .co(somador_completo_2_co));
  somador_completo somador_completo_3 (
    .ci(somador_completo_2_co), .a(in_2[2]), .b(xor_3_out), .s(out_4[2]), .co(somador_completo_3_co));
  somador_completo somador_completo_4 (
    .ci(somador_completo_3_co), .a(in_2[3]), .b(xor_4_out), .s(out_4[3]), .co(somador_completo_4_co));
  somador_completo somador_completo_5 (
    .ci(somador_completo_4_co), .a(in_2[4]), .b(xor_5_out), .s(out_4[4]), .co(somador_completo_5_co));
  somador_completo somador_completo_6 (
    .ci(somador_completo_5_co), .a(in_2[5]), .b(xor_6_out), .s(out_4[5]), .co(somador_completo_6_co));
  somador_completo somador_completo_7 (
    .ci(somador_completo_6_co), .a(in_2[6]), .b(xor_7_out), .s(out_4[6]), .co(somador_completo_7_co));
  somador_completo somador_completo_8 (
    .ci(somador_completo_7_co), .a(in_2[7]), .b(xor_8_out), .s(out_4[7]), .co(somador_completo_8_co));
  xor xor_9 (out_5, somador_completo_8_co, m);
endmodule

module deslocador (
  input  [7:0] entrada,
  input  C,
  output [7:0] saida
);

  wire and_1_out, and_3_out, and_4_out, and_5_out, and_6_out, and_7_out, and_8_out, and_9_out, and_10_out,
       and_11_out, and_13_out, and_14_out, not_1_out;

  not not_1 (not_1_out, C);
  and and_1 (and_1_out, entrada[0], C);
  and and_2 (saida[0], not_1_out, entrada[1]);
  and and_3 (and_3_out, entrada[1], C);
  or or_1 (saida[1], and_1_out, and_5_out);
  and and_4 (and_4_out, entrada[2], C);
  and and_5 (and_5_out, not_1_out, entrada[2]);
  or or_2 (saida[2], and_3_out, and_7_out);
  and and_6 (and_6_out, entrada[3], C);
  and and_7 (and_7_out, not_1_out, entrada[3]);
  or or_3 (saida[3], and_4_out, and_9_out);
  and and_8 (and_8_out, entrada[4], C);
  and and_9 (and_9_out, not_1_out, entrada[4]);
  or or_4 (saida[4], and_6_out, and_10_out);
  and and_10 (and_10_out, not_1_out, entrada[5]);
  and and_11 (and_11_out, entrada[5], C);
  or or_5 (saida[5], and_8_out, and_13_out);
  and and_12 (saida[7], entrada[6], C);
  and and_13 (and_13_out, not_1_out, entrada[6]);
  or or_6 (saida[6], and_11_out, and_14_out);
  and and_14 (and_14_out, not_1_out, entrada[7]);
endmodule

module deslocador_2bits (
  input  [7:0] in_1,
  input  ritgh_left,
  output [7:0] out_3
);

  wire [7:0] deslocador_1_saida;

  deslocador deslocador_1 (.entrada(in_1), .C(ritgh_left), .saida(deslocador_1_saida));
  deslocador deslocador_2 (.entrada(deslocador_1_saida), .C(ritgh_left), .saida(out_3));
endmodule
