// Logisim project 12-Maquina-de-estado.circ as structural Verilog: 2 circuits, main circuit main
module main (
  input  in_1
);

  wire clock_1_out, \semaforo_1_saída ;

  semaforo semaforo_1 (.\SAÍDA (\semaforo_1_saída ), .CLOCK(clock_1_out), .ENTRADA(in_1));
  Clock clock_1 (.out(clock_1_out));
  LED led_1 (.in(\semaforo_1_saída ));
endmodule

module semaforo (
  input  CLOCK,
  input  ENTRADA,
  output \SAÍDA 
);

  wire and_1_out, and_2_out, or_1_out;

  and and_1 (and_1_out, ~\SAÍDA , ENTRADA);  // AND_Gate
  and and_2 (and_2_out, \SAÍDA , ~ENTRADA);  // AND_Gate
  or or_1 (or_1_out, and_1_out, and_2_out);
  flipflop_padrao flipflop_padrao_1 (.set(CLOCK), .reset(or_1_out), .Q(\SAÍDA ));  // open: Q_minus

  // Notes on the sheet:
  //   Maquina de Estado 
endmodule
