// Logisim project 13-ContadorSicrono.circ as structural Verilog: 2 circuits, main circuit contador sincrono
module contador_sincrono (
  input  in_1,
  output out_2,
  output out_3,
  output out_4,
  output out_5
);

  wire and_1_out, and_2_out, clock_1_out;

  Clock clock_1 (.out(clock_1_out));
  flipflop_T flipflop_t_1 (.nPreset(1'b0), .J(1'b1), .nClear(in_1), .Q(out_2), .cllock(clock_1_out));  // open: nQ
  flipflop_T flipflop_t_2 (.nPreset(1'b0), .J(out_2), .nClear(in_1), .Q(out_3), .cllock(clock_1_out));  // open: nQ
  and and_1 (and_1_out, out_2, out_3);
  flipflop_T flipflop_t_3 (.nPreset(1'b0), .J(and_1_out), .nClear(in_1), .Q(out_4), .cllock(clock_1_out));  // open: nQ
  and and_2 (and_2_out, and_1_out, out_4);
  flipflop_T flipflop_t_4 (.nPreset(1'b0), .J(and_2_out), .nClear(in_1), .Q(out_5), .cllock(clock_1_out));  // open: nQ
endmodule

module flipflop_T (
  input  nPreset,
  input  J,
  input  cllock,
  input  nClear,
  output Q,
  output nQ
);

  wire nand_1_out, nand_2_out, nand_3_out, nand_4_out, nand_5_out, nand_8_out, not_1_out, not_2_out,
       not_3_out;

  not not_1 (not_1_out, nPreset);
  nand nand_1 (nand_1_out, nQ, J, cllock);
  not not_2 (not_2_out, cllock);
  not not_3 (not_3_out, nClear);
  nand nand_2 (nand_2_out, cllock, J, Q);
  nand nand_3 (nand_3_out, not_1_out, nand_1_out, nand_4_out);
  nand nand_4 (nand_4_out, nand_3_out, nand_2_out, not_3_out);
  nand nand_5 (nand_5_out, nand_3_out, not_2_out);
  nand nand_6 (Q, nand_5_out, nQ);
  nand nand_7 (nQ, Q, nand_8_out);
  nand nand_8 (nand_8_out, not_2_out, nand_4_out);
endmodule
