// Logisim project 14-Paridade-Impar.circ as structural Verilog: 2 circuits, main circuit main
module main (
  input  [7:0] in_1,
  output out_2
);

  wire xor_1_out_3, xor_2_out_3, xor_3_out_3, xor_4_out_3, xor_5_out_3, xor_7_out_3;

  \xor  xor_1 (.in_1(in_1[0]), .in_2(in_1[1]), .out_3(xor_1_out_3));
  \xor  xor_2 (.in_1(in_1[2]), .in_2(in_1[3]), .out_3(xor_2_out_3));
  \xor  xor_3 (.in_1(in_1[4]), .in_2(in_1[5]), .out_3(xor_3_out_3));
  \xor  xor_4 (.in_1(in_1[6]), .in_2(in_1[7]), .out_3(xor_4_out_3));
  \xor  xor_5 (.in_1(xor_1_out_3), .in_2(xor_2_out_3), .out_3(xor_5_out_3));
  \xor  xor_6 (.in_1(xor_5_out_3), .in_2(xor_7_out_3), .out_3(out_2));
  \xor  xor_7 (.in_1(xor_3_out_3), .in_2(xor_4_out_3), .out_3(xor_7_out_3));
endmodule

module \xor  (
  input  in_1,
  input  in_2,
  output out_3
);

  wire and_1_out, and_2_out;

  and and_1 (and_1_out, in_1, ~in_2);  // AND_Gate
  or or_1 (out_3, and_1_out, and_2_out);
  and and_2 (and_2_out, ~in_1, in_2);  // AND_Gate
endmodule
