// Logisim project 15-Simplificacao.circ as structural Verilog: 1 circuit, main circuit main
module main (
  input  A,
  input  B,
  input  C,
  input  C_2,
  output out_5,
  output out_6
);

  wire and_1_out, and_2_out, and_3_out, and_4_out;

  and and_1 (and_1_out, ~C, ~B, A);  // AND_Gate
  and and_2 (and_2_out, ~C, ~B, ~A);  // AND_Gate
  or or_1 (out_5, and_2_out, and_1_out, and_4_out, and_3_out);
  not not_1 (out_6, C_2);
  and and_3 (and_3_out, ~C, B, A);  // AND_Gate
  and and_4 (and_4_out, ~C, B, ~A);  // AND_Gate

  // Notes on the sheet:
  //   CIRCUITO SIMPLES
  //   S = A'B'C'+ AB'C'+A'BC'+ABC'
  //   CIRCUITO SIMPLIMFICADO
endmodule
