// Logisim project 16-Decodificador-7-Seg-Hex.circ as structural Verilog: 3 circuits, main circuit main
module main (
  input  [3:0] in_1,
  output a,
  output b,
  output c,
  output d,
  output e,
  output f,
  output g
);

  wire decodificador4_16_1_out_2, decodificador4_16_1_out_3, decodificador4_16_1_out_4,
       decodificador4_16_1_out_5, decodificador4_16_1_out_6, decodificador4_16_1_out_7,
       decodificador4_16_1_out_8, decodificador4_16_1_out_9, decodificador4_16_1_out_10,
       decodificador4_16_1_out_11, decodificador4_16_1_out_12, decodificador4_16_1_out_13,
       decodificador4_16_1_out_14, decodificador4_16_1_out_15, decodificador4_16_1_out_16,
       decodificador4_16_1_out_17;

  Decodificador4_16 decodificador4_16_1 (
    .out_2(decodificador4_16_1_out_2), .out_3(decodificador4_16_1_out_3), .out_4(decodificador4_16_1_out_4),
    .out_5(decodificador4_16_1_out_5), .out_6(decodificador4_16_1_out_6), .out_7(decodificador4_16_1_out_7),
    .out_8(decodificador4_16_1_out_8), .out_9(decodificador4_16_1_out_9),
    .out_10(decodificador4_16_1_out_10), .out_11(decodificador4_16_1_out_11),
    .out_12(decodificador4_16_1_out_12), .out_13(decodificador4_16_1_out_13),
    .out_14(decodificador4_16_1_out_14), .out_15(decodificador4_16_1_out_15),
    .out_16(decodificador4_16_1_out_16), .out_17(decodificador4_16_1_out_17), .in_1(in_1));
  or u_A (a, decodificador4_16_1_out_2, decodificador4_16_1_out_4, decodificador4_16_1_out_5, decodificador4_16_1_out_7, decodificador4_16_1_out_8, decodificador4_16_1_out_9, decodificador4_16_1_out_10, decodificador4_16_1_out_11, decodificador4_16_1_out_12, decodificador4_16_1_out_14, decodificador4_16_1_out_16, decodificador4_16_1_out_17);
  or u_B (b, decodificador4_16_1_out_2, decodificador4_16_1_out_3, decodificador4_16_1_out_4, decodificador4_16_1_out_5, decodificador4_16_1_out_6, decodificador4_16_1_out_9, decodificador4_16_1_out_10, decodificador4_16_1_out_11, decodificador4_16_1_out_12, decodificador4_16_1_out_15);
  or u_C (c, decodificador4_16_1_out_2, decodificador4_16_1_out_3, decodificador4_16_1_out_5, decodificador4_16_1_out_6, decodificador4_16_1_out_7, decodificador4_16_1_out_8, decodificador4_16_1_out_9, decodificador4_16_1_out_10, decodificador4_16_1_out_11, decodificador4_16_1_out_12, decodificador4_16_1_out_13, decodificador4_16_1_out_15);
  or u_D (d, decodificador4_16_1_out_2, decodificador4_16_1_out_4, decodificador4_16_1_out_5, decodificador4_16_1_out_7, decodificador4_16_1_out_8, decodificador4_16_1_out_10, decodificador4_16_1_out_11, decodificador4_16_1_out_13, decodificador4_16_1_out_14, decodificador4_16_1_out_15, decodificador4_16_1_out_16);
  or u_E (e, decodificador4_16_1_out_2, decodificador4_16_1_out_4, decodificador4_16_1_out_8, decodificador4_16_1_out_10, decodificador4_16_1_out_12, decodificador4_16_1_out_13, decodificador4_16_1_out_14, decodificador4_16_1_out_15, decodificador4_16_1_out_16, decodificador4_16_1_out_17);
  or u_F (f, decodificador4_16_1_out_2, decodificador4_16_1_out_6, decodificador4_16_1_out_7, decodificador4_16_1_out_8, decodificador4_16_1_out_10, decodificador4_16_1_out_11, decodificador4_16_1_out_12, decodificador4_16_1_out_13, decodificador4_16_1_out_14, decodificador4_16_1_out_16, decodificador4_16_1_out_17);
  or u_G (g, decodificador4_16_1_out_4, decodificador4_16_1_out_5, decodificador4_16_1_out_6, decodificador4_16_1_out_7, decodificador4_16_1_out_8, decodificador4_16_1_out_10, decodificador4_16_1_out_11, decodificador4_16_1_out_12, decodificador4_16_1_out_13, decodificador4_16_1_out_15, decodificador4_16_1_out_16, decodificador4_16_1_out_17);
endmodule

module Decodificador4_16 (
  input  [3:0] in_1,
  output out_2,
  output out_3,
  output out_4,
  output out_5,
  output out_6,
  output out_7,
  output out_8,
  output out_9,
  output out_10,
  output out_11,
  output out_12,
  output out_13,
  output out_14,
  output out_15,
  output out_16,
  output out_17
);

  wire not_1_out, not_2_out, not_3_out, not_4_out;

  not not_1 (not_1_out, in_1[3]);
  not not_2 (not_2_out, in_1[2]);
  not not_3 (not_3_out, in_1[1]);
  not not_4 (not_4_out, in_1[0]);
  and _0 (out_2, not_1_out, not_2_out, not_3_out, not_4_out);
  and _1 (out_3, not_1_out, not_2_out, not_3_out, in_1[0]);
  and _2 (out_4, not_1_out, not_2_out, in_1[1], not_4_out);
  and _3 (out_5, not_1_out, not_2_out, in_1[1], in_1[0]);
  and _4 (out_6, not_1_out, in_1[2], not_3_out, not_4_out);
  and _5 (out_7, not_1_out, in_1[2], not_3_out, in_1[0]);
  and _6 (out_8, not_1_out, in_1[2], in_1[1], not_4_out);
  and _7 (out_9, not_1_out, in_1[2], in_1[1], in_1[0]);
  and _8 (out_10, in_1[3], not_2_out, not_3_out, not_4_out);
  and _9 (out_11, in_1[3], not_2_out, not_3_out, in_1[0]);
  and _10 (out_12, in_1[3], not_2_out, in_1[1], not_4_out);
  and _11 (out_13, in_1[3], not_2_out, in_1[1], in_1[0]);
  and _12 (out_14, in_1[3], in_1[2], not_3_out, not_4_out);
  and _13 (out_15, in_1[3], in_1[2], not_3_out, in_1[0]);
  and _14 (out_16, in_1[3], in_1[2], in_1[1], not_4_out);
  and _15 (out_17, in_1[3], in_1[2], in_1[1], in_1[0]);
endmodule

module Contador_4bits_7Seg (
);

  wire and_1_out, and_2_out, clock_1_out, main_1_a, main_1_b, main_1_c, main_1_d, main_1_e, main_1_f,
       main_1_g;
  wire [3:0] t_ff_1_q;

  Clock clock_1 (.out(clock_1_out));
  T_Flip_Flop #(.trigger("falling")) t_ff_1 (
    .clk(clock_1_out), .T(1'b1), .Q(t_ff_1_q[0]));  // open: Qn, preset, reset, en
  T_Flip_Flop #(.trigger("falling")) t_ff_2 (
    .clk(clock_1_out), .T(t_ff_1_q[0]), .Q(t_ff_1_q[1]));  // open: Qn, preset, reset, en
  and and_1 (and_1_out, t_ff_1_q[1], t_ff_1_q[0]);
  T_Flip_Flop #(.trigger("falling")) t_ff_3 (
    .clk(clock_1_out), .T(and_1_out), .Q(t_ff_1_q[2]));  // open: Qn, preset, reset, en
  and and_2 (and_2_out, t_ff_1_q[2], and_1_out);
  T_Flip_Flop #(.trigger("falling")) t_ff_4 (
    .clk(clock_1_out), .T(and_2_out), .Q(t_ff_1_q[3]));  // open: Qn, preset, reset, en
  main main_1 (
    .in_1(t_ff_1_q), .a(main_1_a), .b(main_1_b), .c(main_1_c), .d(main_1_d), .e(main_1_e), .f(main_1_f),
    .g(main_1_g));
  _7_Segment_Display u_7_segment_display_1 (
    .g(main_1_g), .f(main_1_f), .a(main_1_a), .b(main_1_b), .e(main_1_e), .d(main_1_d), .c(main_1_c));  // open: dp
endmodule
